// Logisim project Milestone2.circ as structural Verilog: 3 circuits, main circuit main
// Main
module main (
  input  in_1,
  input  in_2,
  input  in_3,
  input  in_4,
  output out_5
);

  wire AC__0, ALU1, ALU2, ALU3, ALU4, ALU7, BUS0, BUS1, BUS3, BUS4, BUS5, BUS6, clk, INC_PC, IR0, IR1, IR2,
       IR3, IR4, IR5, IR6, IR7, IR8, IR9, IR10, IR11, IR12, IR13, IR14, IR15, LD_AC, LD_AR, LD_DR, LD_E,
       LD_IR, LD_PC, READ, WRITE;
  wire [2:0] priority_encoder_1_out, priority_encoder_2_out;
  wire [6:0] AR_q, bit_extender_1_out, bit_extender_2_out, pc_q;
  wire [15:0] AC_q, alu_1_ac_output, bit_extender_3_out, bit_extender_4_out, DR_q, multiplexer_1_out,
       ram_1_data, TR_q;

  Clock clock_1 (.out(clk));
  Bit_Extender #(.in_width(16), .out_width(7)) bit_extender_1 (.in(multiplexer_1_out), .out(bit_extender_1_out));
  Bit_Extender #(.in_width(16), .out_width(7)) bit_extender_2 (.in(multiplexer_1_out), .out(bit_extender_2_out));
  Register #(.width(7)) AR (.D(bit_extender_1_out), .en(LD_AR), .Q(AR_q), .clk(clk));  // open: clr
  Register #(.width(16)) TR (.D(multiplexer_1_out), .en(in_1), .Q(TR_q), .clk(clk));  // open: clr
  Register #(.width(16)) DR (.D(multiplexer_1_out), .en(LD_DR), .Q(DR_q), .clk(clk));  // open: clr
  Register #(.width(16)) AC (.D(alu_1_ac_output), .en(LD_AC), .Q(AC_q), .clk(clk));  // open: clr
  Counter #(.width(7), .max('h7f)) pc (
    .load(LD_PC), .D(bit_extender_2_out), .count(INC_PC), .Q(pc_q), .clk(clk));  // open: carry, clr
  Register #(.width(16)) IR (
    .D(multiplexer_1_out), .en(LD_IR),
    .Q({IR15, IR14, IR13, IR12, IR11, IR10, IR9, IR8, IR7, IR6, IR5, IR4, IR3, IR2, IR1, IR0}), .clk(clk));  // open: clr
  RAM #(.addrWidth(7), .dataWidth(16), .bus("separate")) ram_1 (
    .addr(AR_q), .din(multiplexer_1_out), .data(ram_1_data), .str(WRITE), .ld(READ));  // open: sel, clk, clr
  Priority_Encoder priority_encoder_1 (
    .in0(in_2), .in1(ALU1), .in2(ALU2), .in3(ALU3), .in4(ALU4), .in5(in_2), .in6(in_2), .in7(ALU7),
    .out(priority_encoder_1_out));  // open: en_in
  assign bit_extender_3_out = {{9{1'b0}}, AR_q};  // Bit_Extender bit_extender_3
  ALU alu_1 (.A(DR_q), .B(AC_q), .in_3(priority_encoder_1_out), .E(out_5), .AC_Output(alu_1_ac_output));
  assign bit_extender_4_out = {{9{1'b0}}, pc_q};  // Bit_Extender bit_extender_4
  Control_unit control_unit_1 (
    .IR0(IR0), .IR1(IR1), .IR2(IR2), .IR3(IR3), .IR4(IR4), .IR5(IR5), .IR6(IR6), .IR7(IR7), .IR8(IR8),
    .IR9(IR9), .IR10(IR10), .IR11(IR11), .IR12(IR12), .IR13(IR13), .IR14(IR14), .IR15(IR15), .clk(clk),
    .AC____0(AC__0), .BUS6(BUS6), .BUS5(BUS5), .LD_DR(LD_IR), .LD_IR(LD_DR), .LD_E(LD_E), .ALU1(ALU1),
    .ALU2(ALU2), .ALU3(ALU3), .ALU4(ALU4), .LD_AC(LD_AC), .ALU7(ALU7), .LD_AR(LD_AR), .LD_AC_2(LD_AC),
    .LD_PC(LD_PC), .INC_PC(INC_PC), .WRITE(WRITE), .READ(READ), .BUS4(BUS4), .BUS0(BUS0), .BUS1(BUS1),
    .BUS3(BUS3));
  Multiplexer #(.select(3), .width(16), .enable("false")) multiplexer_1 (
    .in0(ram_1_data), .in1(bit_extender_3_out), .in2(TR_q), .in3(DR_q), .in4(AC_q), .in5(bit_extender_4_out),
    .in6({IR15, IR14, IR13, IR12, IR11, IR10, IR9, IR8, IR7, IR6, IR5, IR4, IR3, IR2, IR1, IR0}),
    .out(multiplexer_1_out), .sel(priority_encoder_2_out));  // open: in7
  Priority_Encoder priority_encoder_2 (
    .in0(BUS0), .in1(BUS1), .in2(in_3), .in3(BUS3), .in4(BUS4), .in5(BUS5), .in6(BUS6), .in7(in_4),
    .out(priority_encoder_2_out));  // open: en_in
  and and_1 (AC__0, AC_q[0], AC_q[1], AC_q[2], AC_q[3], AC_q[4], AC_q[5], AC_q[6], AC_q[7], AC_q[9], AC_q[10], AC_q[11], AC_q[12], AC_q[13], AC_q[14], AC_q[15], AC_q[8]);

  // Notes on the sheet:
  //   PC
endmodule

module ALU (
  input  [15:0] A,
  input  [15:0] B,
  input  [2:0] in_3,
  output E,
  output [15:0] AC_Output
);

  wire adder_1_cout, adder_2_cout, subtractor_1_bout;
  wire [15:0] adder_1_out, adder_2_out, and_1_out, or_1_out, subtractor_1_out, xor_1_out;

  Adder #(.width(16)) adder_1 (.a(A), .b(B), .out(adder_1_out), .cin(1'b0), .cout(adder_1_cout));
  Subtractor #(.width(16)) subtractor_1 (.a(A), .b(B), .out(subtractor_1_out), .bin(1'b0), .bout(subtractor_1_bout));
  assign and_1_out = A & B;  // AND_Gate and_1, 16 bits wide
  assign or_1_out = A | B;  // OR_Gate or_1, 16 bits wide
  assign xor_1_out = A ^ B;  // XOR_Gate xor_1, 16 bits wide
  Adder #(.width(16)) adder_2 (.a(A), .b({16{1'b0}}), .out(adder_2_out), .cin(1'b1), .cout(adder_2_cout));
  or or_2 (E, adder_1_cout, subtractor_1_bout, adder_2_cout);
  Multiplexer #(.select(3), .width(16)) multiplexer_1 (
    .in1(adder_1_out), .in2(subtractor_1_out), .in3(A), .in4(and_1_out), .in5(or_1_out), .in6(xor_1_out),
    .in7(adder_2_out), .out(AC_Output), .sel(in_3));  // open: in0, en
endmodule

// CU
module Control_unit (
  input  IR0,
  input  IR1,
  input  IR2,
  input  IR3,
  input  IR4,
  input  IR5,
  input  IR6,
  input  IR7,
  input  IR8,
  input  IR9,
  input  IR10,
  input  IR11,
  input  IR12,
  input  IR13,
  input  IR14,
  input  IR15,
  input  clk,
  input  AC____0,
  output LD_DR,
  output LD_IR,
  output LD_E,
  output ALU1,
  output ALU2,
  output ALU3,
  output ALU4,
  output LD_AC,
  output ALU7,
  output LD_AR,
  output LD_AC_2,
  output LD_PC,
  output INC_PC,
  output WRITE,
  output READ,
  output BUS6,
  output BUS5,
  output BUS4,
  output BUS0,
  output BUS1,
  output BUS3
);

  wire and_2_out, and_3_out, and_8_out, and_9_out, and_10_out, and_11_out, and_12_out, and_13_out,
       and_14_out, and_15_out, and_16_out, and_17_out, and_18_out, and_19_out, and_20_out, and_21_out,
       and_22_out, and_23_out, and_24_out, and_25_out, and_26_out, and_27_out, and_28_out, and_29_out,
       and_30_out, and_31_out, and_32_out, and_33_out, and_38_out, and_39_out, and_40_out, and_41_out,
       and_42_out, and_43_out, and_44_out, and_45_out, and_46_out, D0, D1, D2, D3, D4, D5, D6, D7, d_ff_1_q,
       not_1_out, not_2_out, not_3_out, not_4_out, not_5_out, not_6_out, not_7_out, not_8_out, SC_CLR, T3,
       T4, T5, T6, T7, T8, T9, T10, T11, T12, T13, T14, T15;
  wire [3:0] SC_q;

  not not_1 (not_1_out, IR15);
  Counter #(.width(4), .max('hf)) SC (.count(not_2_out), .Q(SC_q), .clk(clk), .clr(d_ff_1_q));  // open: load, D, carry
  not not_2 (not_2_out, SC_CLR);
  and and_1 (LD_E, D1, T5);
  and and_2 (and_2_out, D2, T5);
  and and_3 (and_3_out, D5, T5);
  not not_3 (not_3_out, IR15);
  Decoder #(.select(3), .enable("false")) decoder_1 (
    .out0(D0), .out1(D1), .out2(D2), .out3(D3), .out4(D4), .out5(D5), .out6(D6), .out7(D7),
    .sel({IR14, IR13, IR12}));
  Decoder #(.select(4), .enable("false")) decoder_2 (
    .out0(BUS5), .out1(LD_IR), .out2(BUS6), .out3(T3), .out4(T4), .out5(T5), .out6(T6), .out7(T7), .out8(T8),
    .out9(T9), .out10(T10), .out11(T11), .out12(T12), .out13(T13), .out14(T14), .out15(T15), .sel(SC_q));
  D_Flip_Flop d_ff_1 (.clk(clk), .D(SC_CLR), .Q(d_ff_1_q));  // open: Qn, preset, en, reset
  and and_4 (ALU1, D1, T5);
  and and_5 (ALU2, D5, T6);
  and and_6 (ALU4, D0, T5);
  and and_7 (ALU7, D7, T4, not_3_out, IR5);
  and and_8 (and_8_out, D3, T4);
  and and_9 (and_9_out, D5, T5);
  and and_10 (and_10_out, D7, T3, IR5, not_1_out);
  or or_1 (ALU3, and_2_out, and_3_out);
  and and_11 (and_11_out, D1, T5);
  and and_12 (and_12_out, D2, T5);
  and and_13 (and_13_out, D5, T5);
  and and_14 (and_14_out, D5, T6);
  not not_4 (not_4_out, IR15);
  and and_15 (and_15_out, T4, not_4_out, IR5, D7);
  or or_2 (BUS4, and_8_out, and_9_out, and_10_out);
  not not_5 (not_5_out, IR15);
  and and_16 (and_16_out, D0, T5);
  and and_17 (and_17_out, D0, T5);
  and and_18 (and_18_out, D1, T5);
  and and_19 (and_19_out, D2, T5);
  and and_20 (and_20_out, D5, T5);
  and and_21 (and_21_out, D5, T6);
  and and_22 (and_22_out, T4, not_5_out, IR5, D7);
  and and_23 (and_23_out, AC____0, D7, T3, IR2, not_6_out);
  not not_6 (not_6_out, IR15);
  and and_24 (and_24_out, D0, T4);
  and and_25 (and_25_out, D1, T4);
  and and_26 (and_26_out, D2, T4);
  and and_27 (and_27_out, D5, T4);
  and and_28 (and_28_out, D1, T4);
  and and_29 (and_29_out, D1, T5);
  and and_30 (and_30_out, D5, T5);
  and and_31 (and_31_out, D5, T4);
  not not_7 (not_7_out, IR15);
  and and_32 (and_32_out, D7, not_7_out, IR5, T3);
  and and_33 (and_33_out, D0, T4);
  or or_3 (LD_AR, BUS5, BUS6);
  and and_34 (BUS3, D2, T5);
  or or_4 (LD_AC_2, and_16_out, and_11_out, and_12_out, and_13_out, and_14_out, and_15_out);
  and and_35 (LD_PC, D4, T4);
  or or_5 (INC_PC, LD_IR, and_23_out);
  and and_36 (WRITE, D3, T4);
  or or_6 (BUS0, and_24_out, and_25_out, and_26_out, and_27_out, LD_IR);
  and and_37 (BUS1, D4, T4);
  buf and_38 (and_38_out, D2);  // AND_Gate
  or or_7 (LD_AC, and_17_out, and_18_out, and_19_out, and_20_out, and_21_out, and_22_out);
  or or_8 (LD_DR, and_33_out, and_28_out, and_29_out, and_38_out, and_30_out, and_31_out, and_32_out);
  not not_8 (not_8_out, IR15);
  and and_39 (and_39_out, D0, T5);
  and and_40 (and_40_out, D1, T5);
  and and_41 (and_41_out, D2, T5);
  and and_42 (and_42_out, D3, T4);
  and and_43 (and_43_out, D4, T4);
  and and_44 (and_44_out, D5, T6);
  and and_45 (and_45_out, D7, not_8_out, T3, IR2);
  and and_46 (and_46_out, D7, T4, IR5, not_8_out);
  or or_9 (SC_CLR, and_39_out, and_40_out, and_41_out, and_42_out, and_43_out, and_44_out, and_46_out, and_45_out);

  assign READ = BUS0;

  // Other names for the same wires on the sheet: T0 = BUS5; T1 = LD_IR; T2 = BUS6
endmodule
